// Logisim project Final Project Wiring Diagram.circ as structural Verilog: 1 circuit, main circuit main
module main (
);


  // Notes on the sheet:
  //   220 Ohms
  //   5V
  //   GREEN
  //   Force
  //   Sensitive
  //   Resistor
  //   PIC32MX150F128D
  //   1
  //   4
  //   16
  //   17
  //   18
  //   20
  //   LED0
  //   LED1
  //   LED2
  //   LED3
  //   LED4
  //   LED5
  //   LED6
  //   LED7
  //   Above LEDs are Yellow
  //   40
  //   39
  //   38
  //   RED
  //   37
  //   36
  //   35
  //   33
  //   32
  //   29
  //   23
  //   22
  //   21
  //   10 kOhms for both here
  //   +
  //   Motor
  //   1
  //   2
  //   3
  //   6
  //   Diagram Legend
  //   -
  //   LED
  //   -
  //   +
  //   Approx of Diode Shape
  //   Resistor
  //   16
  //   1
  //   2
  //   3
  //   4
  //   5
  //   6
  //   7
  //   8
  //   Greyhill 61C
  //   Optical Encoder
  //   5V
  //   L293DNE
  //   Motor Driver
endmodule
