// Logisim project Pre Lab 10.circ as structural Verilog: 1 circuit, main circuit main
module main (
);


  // Notes on the sheet:
  //   P.D.Resistor
  //   FSR
  //   5V
  //   PIC32MX150F128D
  //   40
  //   1
  //   39
  //   37
  //   36
  //   35
  //   29
  //   23
  //   22
  //   18
  //   21
  //   20
  //   LED0
  //   LED1
  //   LED2
  //   LED3
  //   LED4
  //   LED5
  //   LED6
  //   LED7
endmodule
