// Logisim project Pre Lab 4.circ as structural Verilog: 1 circuit, main circuit main
module main (
);

  wire pull_resistor_1_node;

  Pull_Resistor #(.pull(1)) pull_resistor_1 (.node(pull_resistor_1_node));
  Pull_Resistor #(.pull(1)) pull_resistor_2 (.node(pull_resistor_1_node));
  Pull_Resistor #(.pull(1)) pull_resistor_3 (.node(pull_resistor_1_node));
  Pull_Resistor #(.pull(1)) pull_resistor_4 (.node(pull_resistor_1_node));

  // Notes on the sheet:
  //   5V
  //   PIC32MX150F128D
  //   1
  //   40
  //   39
  //   5
  //   6
  //   34
  //   33
  //   32
  //   26
  //   25
  //   24
  //   23
  //   22
  //   21
  //   20
  //   LED 0
  //   LED 1
  //   LED 2
  //   LED 3
  //   0
  //   4
  //   8
  //   C
  //   1
  //   2
  //   5
  //   6
  //   9
  //   A
  //   E
  //   D
  //   3
  //   7
  //   B
  //   F
  //   Pull Up Resistors not necessary
  //   CNPUC Register set to accommodate this
endmodule
