// Logisim project Pre Lab 5.circ as structural Verilog: 1 circuit, main circuit main
module main (
);

  wire nand_1_out, nand_2_out, pull_resistor_1_node, pull_resistor_2_node;

  nand nand_1 (nand_1_out, pull_resistor_1_node, nand_2_out);
  nand nand_2 (nand_2_out, nand_1_out, pull_resistor_2_node);
  Pull_Resistor #(.pull(1)) pull_resistor_1 (.node(pull_resistor_1_node));
  Pull_Resistor #(.pull(1)) pull_resistor_2 (.node(pull_resistor_2_node));

  // Notes on the sheet:
  //   5V
  //   PIC32MX150F128D
  //   40
  //   1
  //   39
  //   37
  //   23
  //   22
  //   21
  //   20
  //   LED0
  //   LED1
  //   LED2
  //   LED3
  //   R = 1k
  //   R = 1k
  //   Switch
endmodule
