// Logisim project Pre Lab 6.circ as structural Verilog: 1 circuit, main circuit main
module main (
);


  // Notes on the sheet:
  //   5V
  //   PIC32MX150F128D
  //   40
  //   1
  //   39
  //   37
  //   33
  //   23
  //   22
  //   21
  //   20
  //   LED0
  //   LED1
  //   LED2
  //   LED3
  //   6
  //   5
  //   4
  //   3
  //   2
  //   1
  //   61C
  //   Optical
  //   Encoder
endmodule
