// Logisim project Pre Lab 7.circ as structural Verilog: 1 circuit, main circuit main
module main (
);


  // Notes on the sheet:
  //   5V
  //   1
  //   PIC32MX150F128D
  //   40
  //   39
  //   32
  //   R
  //   +
  //   AC-1005G-P
  //   -
endmodule
