// Logisim project Pre Lab 8.circ as structural Verilog: 1 circuit, main circuit main
module main (
);

  wire pull_resistor_1_node;

  Pull_Resistor #(.pull(1)) pull_resistor_1 (.node(pull_resistor_1_node));

  // Notes on the sheet:
  //   5V
  //   PIC32MX150F128D
  //   1
  //   40
  //   39
  //   38
  //   37
  //   29
  //   Motor
  //   N.O. Push Button
  //   Approx of Diode Shape
  //   1
  //   2
  //   3
  //   4
  //   5
  //   6
  //   7
  //   8
  //   Vcc2
  //   16
  //   13
  //   12
  //   Vcc1
endmodule
