// Logisim project Pre Lab 9.circ as structural Verilog: 1 circuit, main circuit main
module main (
);


  // Notes on the sheet:
  //   5V
  //   1
  //   16
  //   PIC32MX150F128D
  //   40
  //   39
  //   37
  //   25
  //   24
  //   R
  //   SN74HC595
  //   1
  //   2
  //   3
  //   4
  //   5
  //   6
  //   7
  //   8
  //   LED0
  //   LED1
  //   LED2
  //   LED3
  //   LED4
  //   LED5
  //   LED6
  //   LED7
  //   N.O.
  //   Push
  //   Button
  //   16
  //   15
  //   14
  //   13
  //   12
  //   11
  //   10
endmodule
